# Fritzing sketch arduino (saved by Fritzing 0.9.4)
breadboards: 1

parts:
  元件1 = Arduino Nano (Rev3.0)
  元件2 = BME280 Breakout  # not connected
  DS1 = DS18B20 1-Wire Temperature Sensor [part_number=DS18B20]
  R1 = Resistor [tolerance=±1% resistance=4.7k package=THT]
  LED1 = LEDs [package=led10mm]
  R2 = Resistor [tolerance=±1% resistance=560 package=THT]

nets:
  N1: 元件1.D2, DS1.DQ, R1.Pin_0
  N2: 元件1.D10, R2.Pin_1
  5V: 元件1.5V, DS1.VDD, R1.Pin_1
  N3: DS1.GND, LED1.C
  N4: LED1.A, R2.Pin_0
